# Fritzing sketch Electricty meter (saved by Fritzing 0.9.3b)
breadboards: 1

parts:
  U1 = NodeMCU V1.0
  Mod1 = zmpt101b
  Part3 = Lilypad Battery Connect
  LED1 = LEDs [package=led10mm]
  C1 = Electrolytic Capacitor [capacitance=10μF package="0605 [SMD, electrolytic]"]
  R1 = Resistor [tolerance=±5% resistance=220 package="0402 [SMD]"]
  R2 = Resistor [tolerance=±5% resistance=220 package="0402 [SMD]"]
  R3 = Resistor [tolerance=±5% resistance=220 package="0402 [SMD]"]

nets:
  3V3: U1.3V3, Mod1.VCC
  GND: U1.GND, Mod1.GND, C1.+, R1.Pin_0, R2.Pin_0, R3.Pin_0
  N1: U1.Vin, R1.Pin_1
  N2: U1.A0, Mod1.OUT
  N3: Mod1.N, Part3.-, LED1.C
  N4: Mod1.L, Part3.+, LED1.A
  N5: C1.-, R2.Pin_1

notes:
  SCT-013 Current Sensor

custom parts:
  NodeMCU V1.0: ESP8266 based NodeMCU
  zmpt101b: Single phase ac active output voltate transformer module.
